// Logisim project Arq.circ as structural Verilog: 2 circuits, main circuit main
module main (
);

  wire _15, button_1_out, Control_de_estado_salida_para_el_juego;
  wire [3:0] counter_1_q, counter_2_q, or_1_out, subtractor_1_out;
  wire [14:0] demultiplexer_1_out0, demultiplexer_1_out1, demultiplexer_1_out2, demultiplexer_1_out3,
       demultiplexer_1_out4, demultiplexer_1_out5, demultiplexer_1_out6, demultiplexer_1_out7,
       demultiplexer_1_out8, demultiplexer_1_out9, demultiplexer_1_out10, demultiplexer_1_out11,
       demultiplexer_1_out12, demultiplexer_1_out13, demultiplexer_1_out14, demultiplexer_2_out15;

  assign or_1_out = 4'b0001 | counter_1_q;  // OR_Gate or_1, 4 bits wide
  Control_de_estado Control_de_estado (
    .Entrada_fin_del_juego(_15), .Entrada_del_boton(button_1_out),
    .Salida_para_el_juego(Control_de_estado_salida_para_el_juego));  // open: Salida_invertida
  Button button_1 (.out(button_1_out));
  Counter #(.width(4), .max('hf)) counter_1 (.Q(counter_1_q), .clk(button_1_out));  // open: load, D, count, carry, clr
  DotMatrix #(.matrixcols(15), .matrixrows(15)) dotmatrix_1 (
    .col0(demultiplexer_1_out0), .col1(demultiplexer_1_out1), .col2(demultiplexer_1_out2),
    .col3(demultiplexer_1_out3), .col4(demultiplexer_1_out4), .col5(demultiplexer_1_out5),
    .col6(demultiplexer_1_out6), .col7(demultiplexer_1_out7), .col8(demultiplexer_1_out8),
    .col9(demultiplexer_1_out9), .col10(demultiplexer_1_out10), .col11(demultiplexer_1_out11),
    .col12(demultiplexer_1_out12), .col13(demultiplexer_1_out13), .col14(demultiplexer_1_out14));
  Counter #(.width(4), .max('hf), .trigger("falling")) counter_2 (
    .Q(counter_2_q), .clk(Control_de_estado_salida_para_el_juego));  // open: load, D, count, carry, clr
  Demultiplexer #(.select(4), .width(15)) demultiplexer_1 (
    .out0(demultiplexer_1_out0), .out1(demultiplexer_1_out1), .out2(demultiplexer_1_out2),
    .out3(demultiplexer_1_out3), .out4(demultiplexer_1_out4), .out5(demultiplexer_1_out5),
    .out6(demultiplexer_1_out6), .out7(demultiplexer_1_out7), .out8(demultiplexer_1_out8),
    .out9(demultiplexer_1_out9), .out10(demultiplexer_1_out10), .out11(demultiplexer_1_out11),
    .out12(demultiplexer_1_out12), .out13(demultiplexer_1_out13), .out14(demultiplexer_1_out14),
    .in(demultiplexer_2_out15), .sel(4'b0011));  // open: out15, en
  Demultiplexer #(.select(4), .disabled(0), .enable("false")) demultiplexer_2 (
    .out0(_15), .out1(demultiplexer_2_out15[14]), .out2(demultiplexer_2_out15[13]),
    .out3(demultiplexer_2_out15[12]), .out4(demultiplexer_2_out15[11]), .out5(demultiplexer_2_out15[10]),
    .out6(demultiplexer_2_out15[9]), .out7(demultiplexer_2_out15[8]), .out8(demultiplexer_2_out15[7]),
    .out9(demultiplexer_2_out15[6]), .out10(demultiplexer_2_out15[5]), .out11(demultiplexer_2_out15[4]),
    .out12(demultiplexer_2_out15[3]), .out13(demultiplexer_2_out15[2]), .out14(demultiplexer_2_out15[1]),
    .out15(demultiplexer_2_out15[0]), .in(1'b1), .sel(subtractor_1_out));
  Subtractor #(.width(4)) subtractor_1 (.a(counter_2_q), .b(or_1_out), .out(subtractor_1_out));  // open: bin, bout

  // Notes on the sheet:
  //   Selector de columna del display
  //   MOVIMIENTO SOLO VERTICAL
endmodule

module Control_de_estado (
  input  Entrada_del_boton,
  input  Entrada_fin_del_juego,
  output Salida_invertida,
  output Salida_para_el_juego
);

  wire clock_1_out, d_ff_1_q;

  D_Flip_Flop d_ff_1 (
    .Q(d_ff_1_q), .Qn(Salida_invertida), .preset(Entrada_del_boton), .reset(Entrada_fin_del_juego));  // open: clk, D, en
  Clock clock_1 (.out(clock_1_out));
  and and_1 (Salida_para_el_juego, d_ff_1_q, clock_1_out);
endmodule
